# Fritzing sketch Untitled Sketch (saved by Fritzing 0.9.3b)
breadboards: 1

parts:
  부품1 = Arduino Uno (Rev3)
  LED1 = RGB LED (com. cathode, rgb) [package="5 mm [THT]"]
  U1 = GAS_SENSOR [package=mq-3]
  SG1 = Buzzer 12mm [package=buzzer-ccv-kit]
  DHT1 = DHT11 Humitidy and Temperature Sensor
  U2 = Sharp Dust Sensor [part_number=GP2Y1010AU0F]
  J1 = Basic Servo
  C1 = Capacitor Polarized [package=cpol-radial-100uf-25v]
  R1 = Resistor [tolerance=±5% resistance=220 package="2512 [SMD]"]

nets:
  N1: 부품1.A1, U2.Vo
  N2: 부품1.D8, LED1.common_cathode
  N3: 부품1.D9_PWM, LED1.red_anode
  N4: 부품1.D10_PWM/SS, DHT1.DATA
  N5: 부품1.D0/RX, U2.LED
  N6: 부품1.D2, J1.pulse
  N7: 부품1.D4, SG1.2
  N8: 부품1.D5_PWM, LED1.green_anode
  VCC: 부품1.5V, U1.H2, DHT1.VDD, U2.VCC, J1.vcc, R1.Pin_1
  GND: 부품1.GND, LED1.blue_anode, U1.H1, SG1.1, DHT1.GND, U2.S-GND, J1.gnd, C1.+
  N9: U2.V-LED, R1.Pin_0
  N10: U2.LED-GND, C1.-

custom parts:
  DHT11 Humitidy and Temperature Sensor: DHT11 Humidity and Temperature Sensor
  Sharp Dust Sensor: Sharp GP2Y1010AU0F Dust Sensor
